// Logisim project sequence-detector-1101 .circ as structural Verilog: 1 circuit, main circuit main
module main (
  input  X,
  output out_2
);

  wire clock_1_out, D1_q, D1_qn, DO_q, DO_qn, not_1_out, or_1_out, or_2_out, Q1_prime_Q0_prime_X_out,
       Q1_prime_Q0_X_out, Q1_Q0_prime_out, Q1_Q0_prime_X_prime_out, Q1_Q0_X_out;

  Clock clock_1 (.out(clock_1_out));
  D_Flip_Flop D1 (.clk(clock_1_out), .D(or_1_out), .Q(D1_q), .Qn(D1_qn));  // open: preset, en, reset
  D_Flip_Flop DO (.clk(clock_1_out), .D(or_2_out), .Q(DO_q), .Qn(DO_qn));  // open: preset, en, reset
  not not_1 (not_1_out, X);
  and Q1_Q0_prime (Q1_Q0_prime_out, DO_qn, D1_q);
  and Q1_prime_Q0_X (Q1_prime_Q0_X_out, X, X, D1_qn, DO_q);
  and Q1_Q0_X (Q1_Q0_X_out, D1_q, X, DO_q);
  and Q1_prime_Q0_prime_X (Q1_prime_Q0_prime_X_out, D1_qn, DO_qn, X);
  and Q1_Q0_prime_X_prime (Q1_Q0_prime_X_prime_out, D1_q, DO_qn, not_1_out);
  or or_1 (or_1_out, Q1_Q0_prime_out, Q1_prime_Q0_X_out);
  or or_2 (or_2_out, Q1_Q0_X_out, Q1_prime_Q0_prime_X_out, Q1_Q0_prime_X_prime_out);
  and and_1 (out_2, X, DO_q, D1_q);
endmodule
