// Logisim project synchronous-counter.circ as structural Verilog: 1 circuit, main circuit main
module main (
  output Q2,
  output Q1,
  output Q0
);

  wire clock_1_out, or_1_out, Q2_qn;

  Clock clock_1 (.out(clock_1_out));
  J_K_Flip_Flop u_Q2 (.J(Q1), .clk(clock_1_out), .K(Q1), .Q(Q2), .Qn(Q2_qn));  // open: preset, en, reset
  or or_1 (or_1_out, Q2, Q0);
  J_K_Flip_Flop u_Q1 (.J(or_1_out), .clk(clock_1_out), .K(1'b1), .Q(Q1));  // open: Qn, preset, en, reset
  J_K_Flip_Flop u_Q0 (.J(Q2_qn), .clk(clock_1_out), .K(Q1), .Q(Q0));  // open: Qn, preset, en, reset
endmodule
